// Logisim project Exemplo_0504.circ as structural Verilog: 1 circuit, main circuit main
module main (
);

  wire clock_1_out, clock_2_out, nand_1_out, nand_2_out;

  Clock clock_1 (.out(clock_1_out));
  Clock #(.lowDuration(2)) clock_2 (.out(clock_2_out));
  nand nand_1 (nand_1_out, clock_1_out, clock_1_out, clock_2_out);
  nand nand_2 (nand_2_out, nand_1_out, nand_1_out);
  LED led_1 (.in(nand_2_out));

  // Notes on the sheet:
  //   x
  //   y
  //   a
endmodule
