// Logisim project Exemplo_0505.circ as structural Verilog: 1 circuit, main circuit main
module main (
);

  wire clock_1_out, clock_2_out, nor_1_out, nor_2_out;

  Clock clock_1 (.out(clock_1_out));
  Clock #(.lowDuration(2)) clock_2 (.out(clock_2_out));
  nor nor_1 (nor_1_out, clock_1_out, clock_2_out);
  nor nor_2 (nor_2_out, nor_1_out, nor_1_out);
  LED led_1 (.in(nor_2_out));

  // Notes on the sheet:
  //   x
  //   y
  //   a
endmodule
