// Logisim project Exemplo_0506.circ as structural Verilog: 1 circuit, main circuit main
module main (
);

  wire clock_1_out, clock_2_out, nand_1_out, nand_2_out, nand_3_out, nand_4_out, nand_5_out;

  Clock clock_1 (.out(clock_1_out));
  Clock #(.lowDuration(2)) clock_2 (.out(clock_2_out));
  nand nand_1 (nand_1_out, clock_1_out, clock_1_out);
  nand nand_2 (nand_2_out, clock_2_out, clock_2_out);
  nand nand_3 (nand_3_out, nand_1_out, clock_2_out);
  nand nand_4 (nand_4_out, clock_1_out, nand_2_out);
  nand nand_5 (nand_5_out, nand_3_out, nand_4_out);
  LED led_1 (.in(nand_5_out));

  // Notes on the sheet:
  //   x
  //   y
  //   a
endmodule
