// Logisim project Exemplo_0507.circ as structural Verilog: 1 circuit, main circuit main
module main (
);

  wire clock_1_out, clock_2_out, nor_1_out, nor_2_out, nor_3_out, nor_4_out;

  Clock clock_1 (.out(clock_1_out));
  Clock clock_2 (.out(clock_2_out));
  nor nor_1 (nor_1_out, clock_1_out, clock_2_out);
  nor nor_2 (nor_2_out, clock_1_out, nor_1_out);
  nor nor_3 (nor_3_out, nor_1_out, clock_2_out);
  nor nor_4 (nor_4_out, nor_2_out, nor_3_out);
  LED led_1 (.in(nor_4_out));

  // Notes on the sheet:
  //   x
  //   y
  //   a
endmodule
