// Logisim project Exercicio_10.circ as structural Verilog: 1 circuit, main circuit main
module main (
);

  wire and_1_out, clock_1_out, clock_2_out, clock_3_out, not_1_out, not_2_out, not_3_out, or_1_out;

  Clock clock_1 (.out(clock_1_out));
  Clock clock_2 (.out(clock_2_out));
  Clock clock_3 (.out(clock_3_out));
  not not_1 (not_1_out, clock_1_out);
  not not_2 (not_2_out, clock_2_out);
  not not_3 (not_3_out, clock_3_out);
  or or_1 (or_1_out, not_1_out, not_2_out, not_3_out);
  and and_1 (and_1_out, or_1_out, clock_3_out);
  LED led_1 (.in(and_1_out));

  // Notes on the sheet:
  //   z
  //   y
  //   x
  //   s
endmodule
