// Logisim project Exemplo_0601.circ as structural Verilog: 1 circuit, main circuit main
module main (
);

  wire and_1_out, clock_1_out, clock_2_out, or_1_out;

  Clock clock_1 (.out(clock_1_out));
  Clock clock_2 (.out(clock_2_out));
  and and_1 (and_1_out, clock_2_out, clock_1_out);
  or or_1 (or_1_out, clock_2_out, clock_1_out);
  LED led_1 (.in(and_1_out));
  LED led_2 (.in(or_1_out));

  // Notes on the sheet:
  //   A
  //   B
  //   S0 (AND)
  //   S1 (OR)
endmodule
