// Logisim project Exemplo_0602.circ as structural Verilog: 1 circuit, main circuit main
module main (
);

  wire and_1_out, and_2_out, and_3_out, clock_1_out, clock_2_out, clock_3_out, not_1_out, or_1_out, or_2_out;

  Clock clock_1 (.out(clock_1_out));
  Clock clock_2 (.out(clock_2_out));
  Clock clock_3 (.out(clock_3_out));
  and and_1 (and_1_out, clock_2_out, clock_1_out);
  or or_1 (or_1_out, clock_2_out, clock_1_out);
  not not_1 (not_1_out, clock_3_out);
  and and_2 (and_2_out, and_1_out, clock_3_out);
  and and_3 (and_3_out, not_1_out, not_1_out, or_1_out);
  or or_2 (or_2_out, and_2_out, and_3_out);
  LED led_1 (.in(or_2_out));

  // Notes on the sheet:
  //   A
  //   B
  //   SELEÇÃO (0 = OR, 1 = AND)
  //   E0
  //   E1
  //   S
endmodule
