// Logisim project Exemplo_0603.circ as structural Verilog: 1 circuit, main circuit main
module main (
);

  wire and_1_out, and_2_out, and_3_out, and_4_out, and_5_out, and_6_out, and_7_out, and_8_out, clock_1_out,
       clock_2_out, clock_3_out, clock_4_out, not_1_out, not_2_out, not_3_out, not_4_out, not_5_out,
       or_1_out, or_2_out, or_3_out, or_4_out, or_5_out;

  Clock clock_1 (.out(clock_1_out));
  Clock clock_2 (.out(clock_2_out));
  Clock clock_3 (.out(clock_3_out));
  Clock clock_4 (.out(clock_4_out));
  and and_1 (and_1_out, clock_1_out, clock_2_out);
  or or_1 (or_1_out, clock_2_out, clock_1_out);
  and and_2 (and_2_out, clock_1_out, clock_2_out);
  not not_1 (not_1_out, and_2_out);
  or or_2 (or_2_out, clock_2_out, clock_1_out);
  not not_2 (not_2_out, or_2_out);
  not not_3 (not_3_out, clock_3_out);
  not not_4 (not_4_out, clock_3_out);
  and and_3 (and_3_out, and_1_out, clock_3_out);
  and and_4 (and_4_out, not_3_out, not_3_out, or_1_out);
  and and_5 (and_5_out, not_1_out, clock_3_out);
  and and_6 (and_6_out, not_4_out, not_4_out, not_2_out);
  or or_3 (or_3_out, and_3_out, and_4_out);
  or or_4 (or_4_out, and_5_out, and_6_out);
  and and_7 (and_7_out, or_3_out, not_5_out);
  not not_5 (not_5_out, clock_4_out);
  and and_8 (and_8_out, or_4_out, clock_4_out);
  or or_5 (or_5_out, and_7_out, and_8_out);
  LED led_1 (.in(or_5_out));

  // Notes on the sheet:
  //   A
  //   B
  //   S0
  //   S1
  //   SELEÇÃO (00 = OR, 01 = AND, 10 = NOR, 11 = NAND)
  //   E0
  //   E1
  //   E3
  //   E2
  //   S
endmodule
