// Logisim project Exemplo_0604.circ as structural Verilog: 1 circuit, main circuit main
module main (
);

  wire and_1_out, and_2_out, and_3_out, and_4_out, and_5_out, and_6_out, and_7_out, and_8_out, and_9_out,
       and_10_out, and_11_out, and_12_out, and_13_out, and_14_out, and_15_out, and_16_out, and_17_out,
       and_18_out, and_19_out, and_20_out, and_21_out, clock_1_out, clock_2_out, clock_3_out, clock_4_out,
       clock_5_out, not_1_out, not_2_out, not_3_out, not_4_out, not_5_out, not_6_out, not_7_out, not_8_out,
       not_9_out, not_10_out, not_11_out, not_12_out, not_13_out, not_14_out, not_15_out, not_16_out,
       or_1_out, or_2_out, or_3_out, or_4_out, or_5_out, or_6_out;

  Clock clock_1 (.out(clock_1_out));
  Clock clock_2 (.out(clock_2_out));
  Clock clock_3 (.out(clock_3_out));
  Clock clock_4 (.out(clock_4_out));
  Clock clock_5 (.out(clock_5_out));
  not not_1 (not_1_out, and_1_out);
  and and_1 (and_1_out, clock_1_out, clock_2_out);
  not not_2 (not_2_out, and_2_out);
  and and_2 (and_2_out, clock_1_out, clock_2_out);
  and and_3 (and_3_out, clock_1_out, clock_2_out);
  or or_1 (or_1_out, clock_2_out, clock_1_out);
  and and_4 (and_4_out, clock_1_out, clock_2_out);
  or or_2 (or_2_out, clock_2_out, clock_1_out);
  and and_5 (and_5_out, clock_1_out, not_1_out);
  and and_6 (and_6_out, not_1_out, clock_2_out);
  and and_7 (and_7_out, clock_1_out, not_2_out);
  not not_3 (not_3_out, and_7_out);
  not not_4 (not_4_out, and_8_out);
  and and_8 (and_8_out, not_2_out, clock_2_out);
  not not_5 (not_5_out, and_4_out);
  not not_6 (not_6_out, or_2_out);
  not not_7 (not_7_out, and_5_out);
  not not_8 (not_8_out, and_6_out);
  and and_9 (and_9_out, not_3_out, not_4_out);
  and and_10 (and_10_out, not_7_out, not_8_out);
  not not_9 (not_9_out, and_10_out);
  not not_10 (not_10_out, and_9_out);
  not not_11 (not_11_out, and_11_out);
  and and_11 (and_11_out, not_10_out, not_10_out);
  not not_12 (not_12_out, clock_3_out);
  not not_13 (not_13_out, clock_3_out);
  not not_14 (not_14_out, clock_3_out);
  and and_12 (and_12_out, and_3_out, clock_3_out);
  and and_13 (and_13_out, not_12_out, not_12_out, or_1_out);
  and and_14 (and_14_out, not_5_out, clock_3_out);
  and and_15 (and_15_out, not_13_out, not_13_out, not_6_out);
  and and_16 (and_16_out, not_9_out, clock_3_out);
  and and_17 (and_17_out, not_14_out, not_14_out, not_11_out);
  or or_3 (or_3_out, and_12_out, and_13_out);
  or or_4 (or_4_out, and_14_out, and_15_out);
  or or_5 (or_5_out, and_16_out, and_17_out);
  and and_18 (and_18_out, or_3_out, not_15_out);
  not not_15 (not_15_out, clock_4_out);
  and and_19 (and_19_out, or_4_out, clock_4_out);
  and and_20 (and_20_out, or_5_out, not_16_out);
  not not_16 (not_16_out, clock_5_out);
  and and_21 (and_21_out, or_5_out, clock_5_out);
  or or_6 (or_6_out, and_18_out, and_19_out);
  LED led_1 (.in(or_6_out));
  // OR_Gate or_7 has open pins: in0=and_20_out, in4=and_21_out, out=open

  // Notes on the sheet:
  //   A
  //   B
  //   S0
  //   S1
  //   S2
  //   SELEÇÃO (00 = OR, 01 = AND, 10 = NOR, 11 = NAND)
  //   E0
  //   E1
  //   E2
  //   E3
  //   E4
  //   E5
  //   S
endmodule
